# Fritzing sketch connections (saved by Fritzing 0.9.0b)
breadboards: 1

parts:
  LCD1 = LCD screen
  Part1 = 4x4 Keypad [part_number=101207]
  Part2 = Arduino Mega 2560 (Rev3)
  R1 = Rotary Potentiometer (Small) [maximum_resistance=100kΩ package=THT]

nets:
  VSS: LCD1.VSS, LCD1.R/W, Part2.GND, R1.leg1
  VDD: LCD1.VDD, Part2.5V, R1.leg2
  N1: LCD1.V0, R1.wiper
  N2: LCD1.RS, Part2.A0
  N3: LCD1.E, Part2.A1
  N4: LCD1.DB4, Part2.A2
  N5: LCD1.DB5, Part2.A3
  N6: LCD1.DB6, Part2.A4
  N7: LCD1.DB7, Part2.A5
  N8: LCD1.LED+, Part2.A6
  N9: LCD1.LED-, Part2.A7
  N10: Part1.1, Part2.D2_PWM
  N11: Part1.2, Part2.D3_PWM
  N12: Part1.3, Part2.D4_PWM
  N13: Part1.4, Part2.D5_PWM
  N14: Part1.5, Part2.D6_PWM
  N15: Part1.6, Part2.D7_PWM
  N16: Part1.7, Part2.D8_PWM
  N17: Part1.8, Part2.D9_PWM

custom parts:
  4x4 Keypad: Matrix membrane keypad 4x4
